# Fritzing sketch photomaton (saved by Fritzing 0.9.3b)
circuit board: 8.46667cm x 5.64444cm

parts:
  Composant1 = Arduino Uno (Rev3)
  R1 = Slide Potentiometer [maximum_resistance=2.4kΩ]
  R2 = Slide Potentiometer [maximum_resistance=2.4kΩ]
  R3 = Resistor [tolerance=±5% resistance=1k package=THT]
  R4 = Resistor [tolerance=±5% resistance=1k package=THT]
  S2 = Pushbutton [package="[THT]"]
  S1 = Pushbutton [package="[THT]"]
  R5 = Resistor [tolerance=±5% resistance=2.8k package=THT]
  R6 = Resistor [tolerance=±5% resistance=2.8k package=THT]
  Composant4 = LED Matrix - Serial Interface - Red/Green/Blue
  R7 = Resistor [tolerance=±5% resistance=6.7k package=THT]
  OMRON1 = OMRON PCB Power Relay – G5LE [part_number="G5LE-1\n" package=THT]
  JP1 = Header 2 [package=screwterminal-3.5mm-2_lock]
  R8 = Resistor [tolerance=±5% resistance=320 package=THT]
  JP2 = Header 2 [package=screwterminal-3.5mm-2_lock]

nets:
  N1: Composant1.A0, S2.Pin_3, S2.Pin_4, R6.Pin_0
  N2: Composant1.A1, S1.Pin_3, S1.Pin_4, R5.Pin_0
  N3: Composant1.A2, OMRON1.COIL2
  N4: Composant1.A3, R2.wiper
  N5: Composant1.A4/SDA, R1.wiper
  GND: Composant1.GND, S2.Pin_1, S2.Pin_2, S1.Pin_1, Composant4.GND, R7.Pin_1, OMRON1.COIL1, OMRON1.B, JP1.2, JP2.2
  N6: Composant1.D6_PWM, Composant4.MOSI
  N7: Composant1.5V, R3.Pin_1, R4.Pin_1, R5.Pin_1, R6.Pin_1
  N8: R1.leg1, R2.leg1
  N9: R1.leg2, R3.Pin_0
  N10: R2.leg2, R4.Pin_0
  N11: Composant4.VCC, JP2.1
  N12: R7.Pin_0, JP1.1, R8.Pin_1
  N13: OMRON1.C, R8.Pin_0

notes:
  Vers chargeur USB 5V 2.4A
  Vers chargeur USB 5V 500mA
  Vers Mic+ Jack mâle
  Vers GND Jack mâle
  Bouton au sol
  Bouton façade
  Luminosité
  Couleur
